# Fritzing sketch HarbyGarageDoor (saved by Fritzing 0.9.3b)
circuit board: 8.46667cm x 5.64444cm
breadboards: 1

parts:
  buttonGarageDoor = Pushbutton [package="[THT]"]
  relayMain = Relay [part_number="3V Relay" package=THT]
  reedDoorClosed = Reed switch [package=THT]
  reedDoorOpen = Reed switch [package=THT]
  R1 = Resistor [tolerance=±5% resistance=10k package=THT]
  R2 = Resistor [tolerance=±5% resistance=10k package=THT]
  Microcontroller = Photon

nets:
  N1: buttonGarageDoor.Pin_1, buttonGarageDoor.Pin_2, relayMain.A
  N2: buttonGarageDoor.Pin_3, buttonGarageDoor.Pin_4, relayMain.C1, relayMain.C2, reedDoorClosed.pin_2, reedDoorOpen.pin_2, Microcontroller.A0, Microcontroller.GND
  N3: relayMain.COIL1, R1.Pin_0, R2.Pin_0, Microcontroller.3V3
  N4: reedDoorClosed.pin_1, R1.Pin_1, Microcontroller.D2
  N5: reedDoorOpen.pin_1, R2.Pin_1, Microcontroller.D4
